# Fritzing sketch waterbot_V1 (saved by Fritzing 0.9.3b)
breadboards: 1

parts:
  Raspberry_Pi_1 = Raspberry Pi 3 [part_number=RPI-3-V1.2]
  Q1 = TRANSISTOR_NPN [part_number=BC548 package=to-92]
  R1 = Resistor [tolerance=±5% resistance=1k package=THT]
  M1 = DC Motor
  HLK-PM1 = HLK-PM12 [part_number="12V DC"]
  DIP-Relay1 = DIP-Relay-D31A [part_number=G5LE-14]
  S1 = Reed switch [package=THT]
  S2 = Reed switch [package=THT]
  R2 = Resistor [tolerance=±5% resistance=4.7k package=THT]
  R3 = Resistor [tolerance=±5% resistance=4.7k package=THT]
  Part1 = Thermal Printer

nets:
  3V3: Raspberry_Pi_1.3v3, Raspberry_Pi_1.3V3, DIP-Relay1.COIL1_+, S1.pin_1, S2.pin_1
  N1: Raspberry_Pi_1.GIPO26, R1.Pin_1
  N2: Raspberry_Pi_1.GIPO16, S1.pin_2, R3.Pin_0
  N3: Raspberry_Pi_1.GIPO12, S2.pin_2, R2.Pin_0
  N4: Raspberry_Pi_1.GND, Q1.E, HLK-PM1.-Vo, DIP-Relay1.A2_Switch_Terminal_A, R2.Pin_1, R3.Pin_1, Part1.GND#2
  N5: Raspberry_Pi_1.GIPO14, Part1.RXD
  N6: Raspberry_Pi_1.5V, DIP-Relay1.A1_Switch_Terminal_A
  N7: Q1.B, R1.Pin_0
  N8: Q1.C, DIP-Relay1.Coil2_-
  N9: M1.pin_1, HLK-PM1.+Vo
  N10: M1.pin_2, DIP-Relay1.B2_Switch_Terminal_B

notes:
  Water Full sensor
  Water Empty sensor
  Water Full
  Water Empty
  Pump
  5V DC
  connect to 5V DC
